// Logisim project tce.circ as structural Verilog: 14 circuits, main circuit main
module main (
);

  wire cte_cu_1_p10, cte_cu_1_p11, cte_cu_1_p12, cte_cu_1_p13, dipswitch_1_sw1, dipswitch_1_sw2,
       dipswitch_1_sw3, dipswitch_1_sw4, dipswitch_1_sw5, dipswitch_1_sw6, dipswitch_1_sw7, dipswitch_1_sw8,
       dipswitch_2_sw4, dipswitch_2_sw5, dipswitch_2_sw6, dipswitch_2_sw7, dipswitch_2_sw8,
       mem_new_big_1_p16, mem_new_big_1_p18, mem_new_big_1_p20, mem_new_big_1_p22, mem_new_big_1_p32,
       mem_new_big_1_p33, mem_new_big_1_p34, mem_new_big_1_p35, mem_new_big_1_p36, mem_new_big_1_p37,
       mem_new_big_1_p38, mem_new_big_1_p39, mem_new_big_1_p40, register_1_q0, register_1_q1, register_1_q2,
       register_1_q3, register_1_q4, register_1_q5, register_1_q6, register_1_q7;

  DipSwitch dipswitch_1 (
    .sw1(dipswitch_1_sw1), .sw2(dipswitch_1_sw2), .sw3(dipswitch_1_sw3), .sw4(dipswitch_1_sw4),
    .sw5(dipswitch_1_sw5), .sw6(dipswitch_1_sw6), .sw7(dipswitch_1_sw7), .sw8(dipswitch_1_sw8));
  // mem_new_big mem_new_big_1: pin names not known; wires that end beside it: dipswitch_1_sw1, dipswitch_1_sw1, dipswitch_1_sw1, dipswitch_1_sw1, dipswitch_1_sw1, dipswitch_1_sw1, dipswitch_1_sw1, dipswitch_1_sw1, dipswitch_1_sw1, dipswitch_1_sw1, dipswitch_1_sw1, dipswitch_1_sw1, dipswitch_1_sw1, dipswitch_1_sw1, dipswitch_1_sw1, mem_new_big_1_p16, mem_new_big_1_p16, mem_new_big_1_p18, mem_new_big_1_p18, mem_new_big_1_p20, mem_new_big_1_p20, mem_new_big_1_p22, mem_new_big_1_p22, dipswitch_1_sw8, dipswitch_1_sw7, dipswitch_1_sw6, dipswitch_1_sw5, dipswitch_1_sw4, dipswitch_1_sw3, dipswitch_1_sw2, dipswitch_1_sw1, mem_new_big_1_p32, mem_new_big_1_p33, mem_new_big_1_p34, mem_new_big_1_p35, mem_new_big_1_p36, mem_new_big_1_p37, mem_new_big_1_p38, mem_new_big_1_p39, mem_new_big_1_p40
  DipSwitch dipswitch_2 (
    .sw1(mem_new_big_1_p38), .sw2(mem_new_big_1_p39), .sw3(mem_new_big_1_p40), .sw4(dipswitch_2_sw4),
    .sw5(dipswitch_2_sw5), .sw6(dipswitch_2_sw6), .sw7(dipswitch_2_sw7), .sw8(dipswitch_2_sw8));
  register register_1 (
    .en_input(cte_cu_1_p12), .clock(mem_new_big_1_p32), .D0(mem_new_big_1_p33), .D1(mem_new_big_1_p34),
    .D2(mem_new_big_1_p35), .D3(mem_new_big_1_p36), .D4(mem_new_big_1_p37), .en_output(1'b1),
    .Q0(register_1_q0), .Q1(register_1_q1), .Q2(register_1_q2), .Q3(register_1_q3), .Q4(register_1_q4),
    .Q5(register_1_q5), .Q6(register_1_q6), .Q7(register_1_q7));  // open: D5, D6, D7, out_12, out_13, out_14, out_15, out_16, out_17, out_18, DG0
  Clock clock_1 (.out(mem_new_big_1_p32));
  // cte_cu cte_cu_1: pin names not known; wires that end beside it: register_1_q0, register_1_q1, register_1_q2, register_1_q3, register_1_q4, register_1_q5, register_1_q6, register_1_q7, mem_new_big_1_p32, cte_cu_1_p10, cte_cu_1_p11, cte_cu_1_p12, cte_cu_1_p13
endmodule

module register (
  input  D0,
  input  D1,
  input  D2,
  input  D3,
  input  D4,
  input  D5,
  input  D6,
  input  D7,
  input  en_input,
  input  clock,
  input  en_output,
  output out_12,
  output out_13,
  output out_14,
  output out_15,
  output out_16,
  output out_17,
  output out_18,
  output DG0,
  output Q0,
  output Q1,
  output Q2,
  output Q3,
  output Q4,
  output Q5,
  output Q6,
  output Q7
);

  Register #(.width(1)) register_1 (.D(D0), .en(en_input), .clk(clock), .Q(DG0));  // open: clr
  Register #(.width(1)) register_2 (.D(D1), .en(en_input), .clk(clock), .Q(out_18));  // open: clr
  Register #(.width(1)) register_3 (.D(D2), .en(en_input), .clk(clock), .Q(out_17));  // open: clr
  Register #(.width(1)) register_4 (.D(D3), .en(en_input), .clk(clock), .Q(out_16));  // open: clr
  Register #(.width(1)) register_5 (.D(D4), .en(en_input), .clk(clock), .Q(out_15));  // open: clr
  Register #(.width(1)) register_6 (.D(D5), .en(en_input), .clk(clock), .Q(out_14));  // open: clr
  Register #(.width(1)) register_7 (.D(D6), .en(en_input), .clk(clock), .Q(out_13));  // open: clr
  Register #(.width(1)) register_8 (.D(D7), .en(en_input), .clk(clock), .Q(out_12));  // open: clr
  assign Q0 = en_output ? DG0 : 1'bz;  // Controlled_Buffer controlled_buffer_1
  assign Q1 = en_output ? out_18 : 1'bz;  // Controlled_Buffer controlled_buffer_2
  assign Q2 = en_output ? out_17 : 1'bz;  // Controlled_Buffer controlled_buffer_3
  assign Q3 = en_output ? out_16 : 1'bz;  // Controlled_Buffer controlled_buffer_4
  assign Q4 = en_output ? out_15 : 1'bz;  // Controlled_Buffer controlled_buffer_5
  assign Q5 = en_output ? out_14 : 1'bz;  // Controlled_Buffer controlled_buffer_6
  assign Q6 = en_output ? out_13 : 1'bz;  // Controlled_Buffer controlled_buffer_7
  assign Q7 = en_output ? out_12 : 1'bz;  // Controlled_Buffer controlled_buffer_8
endmodule

module memory (
  input  A7,
  input  in_2,
  input  in_3,
  input  in_4,
  input  in_5,
  input  in_6,
  input  in_7,
  input  A0,
  input  D0,
  input  in_10,
  input  in_11,
  input  in_12,
  input  in_13,
  input  in_14,
  input  in_15,
  input  D7,
  input  clock,
  input  en_read,
  input  en_write,
  output Q0,
  output out_21,
  output out_22,
  output out_23,
  output out_24,
  output out_25,
  output out_26,
  output Q7
);

  wire [7:0] ram_1_dout;

  RAM ram_1 (
    .addr({A7, in_2, in_3, in_4, in_5, in_6, in_7, A0}), .we(en_write), .oe(en_read), .clk(clock),
    .din({D7, in_15, in_14, in_13, in_12, in_11, in_10, D0}), .dout(ram_1_dout));
  assign {Q7, out_26, out_25, out_24, out_23, out_22, out_21, Q0} = en_read ? ram_1_dout : 8'bz;  // Controlled_Buffer controlled_buffer_1
endmodule

module pc (
  input  [7:0] A,
  input  enabled,
  input  reset,
  input  jump,
  input  count,
  input  clock,
  output out_7,
  output out_8,
  output out_9,
  output out_10,
  output out_11,
  output out_12,
  output out_13,
  output out_14,
  output [7:0] O
);

  Counter counter_1 (
    .clr(reset), .load(jump), .up(1'b1), .count(count), .clk(clock), .D(A),
    .Q({out_7, out_8, out_9, out_10, out_11, out_12, out_13, out_14}));  // open: carry
  assign O = enabled ? {out_7, out_8, out_9, out_10, out_11, out_12, out_13, out_14} : 8'bz;  // Controlled_Buffer controlled_buffer_1
endmodule

module decoder (
  input  D0,
  input  in_2,
  input  in_3,
  input  in_4,
  output out_5,
  output out_6,
  output out_7,
  output out_8,
  output out_9,
  output out_10,
  output out_11,
  output out_12,
  output out_13,
  output out_14,
  output out_15,
  output out_16,
  output out_17,
  output out_18,
  output out_19,
  output out_20
);

  wire not_1_out, not_2_out, not_3_out, not_4_out;

  not not_1 (not_1_out, D0);
  not not_2 (not_2_out, in_2);
  not not_3 (not_3_out, in_3);
  not not_4 (not_4_out, in_4);
  and and_1 (out_20, not_1_out, not_2_out, not_3_out, not_4_out);
  and and_2 (out_19, D0, not_2_out, not_3_out, not_4_out);
  and and_3 (out_18, not_1_out, in_2, not_3_out, not_4_out);
  and and_4 (out_17, D0, in_2, not_3_out, not_4_out);
  and and_5 (out_16, not_1_out, not_2_out, in_3, not_4_out);
  and and_6 (out_15, D0, not_2_out, in_3, not_4_out);
  and and_7 (out_14, not_1_out, in_2, in_3, not_4_out);
  and and_8 (out_13, D0, in_2, in_3, not_4_out);
  and and_9 (out_12, not_1_out, not_2_out, not_3_out, in_4);
  and and_10 (out_11, D0, not_2_out, not_3_out, in_4);
  and and_11 (out_10, not_1_out, in_2, not_3_out, in_4);
  and and_12 (out_9, D0, in_2, not_3_out, in_4);
  and and_13 (out_8, not_1_out, not_2_out, in_3, in_4);
  and and_14 (out_7, D0, not_2_out, in_3, in_4);
  and and_15 (out_6, not_1_out, in_2, in_3, in_4);
  and and_16 (out_5, D0, in_2, in_3, in_4);
endmodule

module clk (
  input  HALT,
  output DEBUG,
  output CLOCK_SIGNAL
);

  wire clock_1_out, not_1_out;

  Clock clock_1 (.out(clock_1_out));
  and and_1 (CLOCK_SIGNAL, clock_1_out, not_1_out);
  not not_1 (not_1_out, HALT);

  assign DEBUG = CLOCK_SIGNAL;
endmodule

module cte_cu (
  input  [7:0] FLAGS,
  input  [4:0] INSTRUCTION,
  input  clock,
  output CTRL,
  output CTRL_1,
  output CTRL_2,
  output CTRL_3,
  output CTRL_4,
  output CTRL_5,
  output CTRL_6,
  output CTRL_7,
  output CTRL_8,
  output CTRL_9,
  output CTRL_10,
  output CTRL_11,
  output CTRL_12,
  output CTRL_13,
  output CTRL_14,
  output CTRL_15,
  output CTRL_16,
  output CTRL_17,
  output CTRL_18,
  output CTRL_19,
  output CTRL_20,
  output CTRL_21,
  output CTRL_22,
  output CTRL_23,
  output CTRL_24,
  output CTRL_25,
  output T,
  output CTRL_26,
  output T_1,
  output CTRL_27,
  output T_2,
  output CTRL_28,
  output T_3,
  output CTRL_29,
  output T_4,
  output CTRL_30,
  output T_5,
  output CTRL_31,
  output T_6,
  output T_7
);

  wire and_1_out, d_ff_1_q, JUMP, n74138_1_pin1, n74138_1_pin2, n74138_1_pin3, n74138_1_pin4, n74138_1_pin6,
       not_1_out, not_2_out, STEP_RESET;
  wire [3:0] MICROCODE_ROM_data;
  wire [7:5] counter_8_bits_1_o0;

  not not_1 (not_1_out, n74138_1_pin6);
  D_Flip_Flop d_ff_1 (.D(STEP_RESET), .clk(not_2_out), .Q(d_ff_1_q), .reset(T));  // open: Qn, preset
  not not_2 (not_2_out, clock);
  and and_1 (and_1_out, d_ff_1_q, not_2_out);
  Counter_8_bits counter_8_bits_1 (
    .COut(n74138_1_pin6), .CEnable(n74138_1_pin6), .CWrite(not_1_out), .CReset(and_1_out), .Clock(not_2_out),
    .out_19(counter_8_bits_1_o0[7]), .out_20(counter_8_bits_1_o0[6]), .O0(counter_8_bits_1_o0[5]));  // open: I7, in_7, in_8, in_9, in_10, in_11, in_12, I0, O7, out_15, out_16, out_17, out_18
  ROM #(.dataWidth(32)) MICROCODE_ROM (
    .addr({counter_8_bits_1_o0, INSTRUCTION}),
    .data({CTRL, CTRL_1, CTRL_2, CTRL_3, CTRL_4, CTRL_5, CTRL_6, CTRL_7, CTRL_8, CTRL_9, CTRL_10, CTRL_11, CTRL_12, CTRL_13, CTRL_14, CTRL_15, CTRL_16, CTRL_17, CTRL_18, CTRL_19, CTRL_20, CTRL_21, CTRL_22, CTRL_23, CTRL_24, CTRL_25, STEP_RESET, JUMP, MICROCODE_ROM_data}));
  _74138 u_74138_1 (
    .pin1(n74138_1_pin1), .pin2(n74138_1_pin2), .pin3(n74138_1_pin3), .pin4(n74138_1_pin4),
    .pin5(n74138_1_pin4), .pin6(n74138_1_pin6), .pin7(T), .pin15(T_7), .pin14(T_6), .pin13(T_5), .pin12(T_4),
    .pin11(T_3), .pin10(T_2), .pin9(T_1));
  not not_3 (n74138_1_pin1, counter_8_bits_1_o0[5]);
  not not_4 (n74138_1_pin2, counter_8_bits_1_o0[6]);
  not not_5 (n74138_1_pin3, counter_8_bits_1_o0[7]);
  LedBar ledbar_1 (.led0(T_7), .led1(T_6), .led2(T_5), .led3(T_4), .led4(T_3), .led5(T_2), .led6(T_1), .led7(T));
  // also tied to GND on the sheet: n74138_1_pin4
  // also tied to VCC on the sheet: n74138_1_pin6

  // Other names for the same wires on the sheet: OUT_READ = CTRL_25; OUT_WRITE = CTRL_24; IN_READ = CTRL_23;
  //   IN_WRITE = CTRL_22; ADDR_READ = CTRL_21; ADDR_WRITE = CTRL_20; DATA_READ = CTRL_19; DATA_WRITE = CTRL_18;
  //   I_READ = CTRL_17; I_WRITE = CTRL_16; A_READ = CTRL_15; A_WRITE = CTRL_14; Y_READ = CTRL_13; Y_WRITE = CTRL_12;
  //   X_READ = CTRL_11; X_WRITE = CTRL_10; MEM_READ = CTRL_9; MEM_WRITE = CTRL_8; ALU_CTRL2 = CTRL_7;
  //   ALU_CTRL1 = CTRL_6; ALU_CTRL0 = CTRL_5; ALU_EN = CTRL_4; PC_JUMP = CTRL_3; PC_COUNT = CTRL_2; PC_EN = CTRL_1;
  //   HALT = CTRL; CARRY_FLAG = FLAGS[0]; ZERO_FLAG = FLAGS[1]; T0 = T; T1 = T_1; T2 = T_2; T3 = T_3; T4 = T_4;
  //   T5 = T_5; T6 = T_6; T7 = T_7

  // Notes on the sheet:
  //   contents of MICROCODE_ROM (hex, n*v repeats v):
  //   32*40408000 16*20004000 16*0 20000020 80000020 0 0 0 20100020 0 20040020 20010020 28160020 2c160020
  //   2a160020 2b160020 29160020 2d120020 20000000 20000320 200000e0 29*0 40400800 31*0 10030
endmodule

module bus_transceiver (
  input  D0,
  input  D1,
  input  D2,
  input  D3,
  input  D4,
  input  D5,
  input  D6,
  input  D7,
  input  BUS_ENABLE,
  output Q0,
  output Q1,
  output Q2,
  output Q3,
  output Q4,
  output Q5,
  output Q6,
  output Q7
);

  assign Q0 = BUS_ENABLE ? D0 : 1'bz;  // Controlled_Buffer controlled_buffer_1
  assign Q1 = BUS_ENABLE ? D1 : 1'bz;  // Controlled_Buffer controlled_buffer_2
  assign Q2 = BUS_ENABLE ? D2 : 1'bz;  // Controlled_Buffer controlled_buffer_3
  assign Q3 = BUS_ENABLE ? D3 : 1'bz;  // Controlled_Buffer controlled_buffer_4
  assign Q4 = BUS_ENABLE ? D4 : 1'bz;  // Controlled_Buffer controlled_buffer_5
  assign Q5 = BUS_ENABLE ? D5 : 1'bz;  // Controlled_Buffer controlled_buffer_6
  assign Q6 = BUS_ENABLE ? D6 : 1'bz;  // Controlled_Buffer controlled_buffer_7
  assign Q7 = BUS_ENABLE ? D7 : 1'bz;  // Controlled_Buffer controlled_buffer_8
endmodule

module tce (
  input  IN7,
  input  in_2,
  input  in_3,
  input  in_4,
  input  in_5,
  input  in_6,
  input  in_7,
  input  IN0,
  output O7,
  output out_10,
  output out_11,
  output out_12,
  output out_13,
  output out_14,
  output out_15,
  output O0
);

  wire alu_1_carry_flag, alu_1_zero_flag, button_1_out, clk_1_clock_signal, clk_1_debug, cte_cu_1_p4,
       cte_cu_1_p5, cte_cu_1_p6, cte_cu_1_p7, cte_cu_1_p8, cte_cu_1_p9, cte_cu_1_p10, cte_cu_1_p11,
       cte_cu_1_p14, cte_cu_1_p15, cte_cu_1_p16, cte_cu_1_p17, cte_cu_1_p18, cte_cu_1_p19, cte_cu_1_p21,
       cte_cu_1_p22, cte_cu_1_p23, cte_cu_1_p24, cte_cu_1_p25, cte_cu_1_p26, cte_cu_1_p27, cte_cu_1_p28,
       cte_cu_1_p29, cte_cu_1_p30, cte_cu_1_p31, cte_cu_1_p32, cte_cu_1_p33, cte_cu_1_p34, cte_cu_1_p35,
       cte_cu_1_p36, cte_cu_1_p37, cte_cu_1_p38, cte_cu_1_p39, cte_cu_1_p40, cte_cu_1_p41, cte_cu_1_p42,
       cte_cu_1_p43, mem_new_big_1_p22, mem_new_big_1_p24, mem_new_big_1_p25, pc_1_out_7, pc_1_out_8,
       pc_1_out_9, pc_1_out_10, pc_1_out_11, pc_1_out_12, pc_1_out_13, pc_1_out_14, register_1_dg0,
       register_1_out_12, register_1_out_13, register_1_out_14, register_1_out_15, register_1_out_16,
       register_1_out_17, register_1_out_18, register_2_dg0, register_2_out_12, register_2_out_13,
       register_2_out_14, register_2_out_15, register_2_out_16, register_2_out_17, register_2_out_18,
       register_3_dg0, register_3_out_12, register_3_out_13, register_3_out_14, register_3_out_15,
       register_3_out_16, register_3_out_17, register_3_out_18, register_4_dg0, register_4_out_12,
       register_4_out_13, register_4_out_14, register_4_out_15, register_4_out_16, register_4_out_17,
       register_4_out_18, register_5_dg0, register_5_out_12, register_5_out_13, register_5_out_14,
       register_5_out_15, register_5_out_16, register_5_out_17, register_5_out_18, register_6_dg0,
       register_6_out_12, register_6_out_13, register_6_out_14, register_6_out_15, register_6_out_16,
       register_6_out_17, register_6_out_18, register_7_dg0, register_7_out_12, register_7_out_13,
       register_7_out_14, register_7_out_15, register_7_out_16, register_7_out_17, register_7_out_18,
       register_8_dg0, register_8_out_12, register_8_out_13, register_8_out_14, register_8_out_15,
       register_8_out_16, register_8_out_17, register_8_out_18, register_9_dg0, register_9_out_12,
       register_9_out_13, register_9_out_14, register_9_out_15, register_9_out_16, register_9_out_17,
       register_9_out_18;
  wire [4:0] register_1_q0;
  wire [5:5] mem_new_big_1_p23;
  wire [7:0] pc_1_o, register_2_q0, register_8_q0, undriven;

  LedBar ledbar_1 (
    .led0(pc_1_o[7]), .led1(pc_1_o[6]), .led2(pc_1_o[5]), .led3(pc_1_o[4]), .led4(pc_1_o[3]),
    .led5(pc_1_o[2]), .led6(pc_1_o[1]), .led7(pc_1_o[0]));
  LedBar #(.matrixcols(1)) ledbar_2 (.led0(clk_1_clock_signal));
  LedBar ledbar_3 (
    .led0(register_2_q0[7]), .led1(register_2_q0[6]), .led2(register_2_q0[5]), .led3(register_2_q0[4]),
    .led4(register_2_q0[3]), .led5(register_2_q0[2]), .led6(register_2_q0[1]), .led7(register_2_q0[0]));
  LED led_1 (.in(clk_1_debug));
  clk clk_1 (.HALT(cte_cu_1_p4), .DEBUG(clk_1_debug), .CLOCK_SIGNAL(clk_1_clock_signal));
  pc pc_1 (
    .clock(clk_1_clock_signal), .enabled(cte_cu_1_p5), .A(pc_1_o), .reset(button_1_out), .jump(cte_cu_1_p7),
    .count(cte_cu_1_p6), .out_7(pc_1_out_7), .out_8(pc_1_out_8), .out_9(pc_1_out_9), .out_10(pc_1_out_10),
    .out_11(pc_1_out_11), .out_12(pc_1_out_12), .out_13(pc_1_out_13), .out_14(pc_1_out_14), .O(pc_1_o));
  LedBar ledbar_4 (
    .led0(pc_1_out_7), .led1(pc_1_out_8), .led2(pc_1_out_9), .led3(pc_1_out_10), .led4(pc_1_out_11),
    .led5(pc_1_out_12), .led6(pc_1_out_13), .led7(pc_1_out_14));
  LedBar ledbar_5 (
    .led0(register_1_out_12), .led1(register_1_out_13), .led2(register_1_out_14), .led3(register_1_out_15),
    .led4(register_1_out_16), .led5(register_1_out_17), .led6(register_1_out_18), .led7(register_1_dg0));
  register register_1 (
    .en_input(mem_new_big_1_p22), .clock(clk_1_clock_signal), .D0(register_2_q0[0]), .D1(register_2_q0[1]),
    .D2(register_2_q0[2]), .D3(register_2_q0[3]), .D4(register_2_q0[4]), .D5(register_2_q0[5]),
    .D6(register_2_q0[6]), .D7(register_2_q0[7]), .en_output(1'b1), .Q0(register_1_q0[0]),
    .Q1(register_1_q0[1]), .Q2(register_1_q0[2]), .Q3(register_1_q0[3]), .Q4(register_1_q0[4]),
    .out_12(register_1_out_12), .out_13(register_1_out_13), .out_14(register_1_out_14),
    .out_15(register_1_out_15), .out_16(register_1_out_16), .out_17(register_1_out_17),
    .out_18(register_1_out_18), .DG0(register_1_dg0));  // open: Q5, Q6, Q7
  LedBar ledbar_6 (
    .led0(register_2_out_12), .led1(register_2_out_13), .led2(register_2_out_14), .led3(register_2_out_15),
    .led4(register_2_out_16), .led5(register_2_out_17), .led6(register_2_out_18), .led7(register_2_dg0));
  register register_2 (
    .en_input(cte_cu_1_p26), .clock(clk_1_clock_signal), .D0(IN0), .D1(in_7), .D2(in_6), .D3(in_5),
    .D4(in_4), .D5(in_3), .D6(in_2), .D7(IN7), .en_output(cte_cu_1_p27), .Q0(register_2_q0[0]),
    .Q1(register_2_q0[1]), .Q2(register_2_q0[2]), .Q3(register_2_q0[3]), .Q4(register_2_q0[4]),
    .Q5(register_2_q0[5]), .Q6(register_2_q0[6]), .Q7(register_2_q0[7]), .out_12(register_2_out_12),
    .out_13(register_2_out_13), .out_14(register_2_out_14), .out_15(register_2_out_15),
    .out_16(register_2_out_16), .out_17(register_2_out_17), .out_18(register_2_out_18), .DG0(register_2_dg0));
  LedBar ledbar_7 (
    .led0(register_3_out_12), .led1(register_3_out_13), .led2(register_3_out_14), .led3(register_3_out_15),
    .led4(register_3_out_16), .led5(register_3_out_17), .led6(register_3_out_18), .led7(register_3_dg0));
  register register_3 (
    .en_input(cte_cu_1_p28), .clock(clk_1_clock_signal), .D0(register_2_q0[0]), .D1(register_2_q0[1]),
    .D2(register_2_q0[2]), .D3(register_2_q0[3]), .D4(register_2_q0[4]), .D5(register_2_q0[5]),
    .D6(register_2_q0[6]), .D7(register_2_q0[7]), .en_output(cte_cu_1_p30), .Q0(O0), .Q1(out_15),
    .Q2(out_14), .Q3(out_13), .Q4(out_12), .Q5(out_11), .Q6(out_10), .Q7(O7), .out_12(register_3_out_12),
    .out_13(register_3_out_13), .out_14(register_3_out_14), .out_15(register_3_out_15),
    .out_16(register_3_out_16), .out_17(register_3_out_17), .out_18(register_3_out_18), .DG0(register_3_dg0));
  Button button_1 (.out(button_1_out));
  LedBar ledbar_8 (
    .led0(register_4_out_12), .led1(register_4_out_13), .led2(register_4_out_14), .led3(register_4_out_15),
    .led4(register_4_out_16), .led5(register_4_out_17), .led6(register_4_out_18), .led7(register_4_dg0));
  register register_4 (
    .en_input(cte_cu_1_p14), .clock(clk_1_clock_signal), .D0(register_2_q0[0]), .D1(register_2_q0[1]),
    .D2(register_2_q0[2]), .D3(register_2_q0[3]), .D4(register_2_q0[4]), .D5(register_2_q0[5]),
    .D6(register_2_q0[6]), .D7(register_2_q0[7]), .en_output(cte_cu_1_p15), .Q0(register_2_q0[0]),
    .Q1(register_2_q0[1]), .Q2(register_2_q0[2]), .Q3(register_2_q0[3]), .Q4(register_2_q0[4]),
    .Q5(register_2_q0[5]), .Q6(register_2_q0[6]), .Q7(register_2_q0[7]), .out_12(register_4_out_12),
    .out_13(register_4_out_13), .out_14(register_4_out_14), .out_15(register_4_out_15),
    .out_16(register_4_out_16), .out_17(register_4_out_17), .out_18(register_4_out_18), .DG0(register_4_dg0));
  // mem_new_big mem_new_big_1: pin names not known; wires that end beside it: register_2_q0[0], register_2_q0[1], register_2_q0[2], register_2_q0[3], register_2_q0[4], register_2_q0[6], register_2_q0[7], register_2_q0[0], register_2_q0[1], register_2_q0[2], register_2_q0[3], register_2_q0[4], register_2_q0[5], register_2_q0[6], register_2_q0[7], register_2_q0[5], clk_1_clock_signal, pc_1_o[1], pc_1_o[3], pc_1_o[5], pc_1_o[7], mem_new_big_1_p22, mem_new_big_1_p23[5], mem_new_big_1_p24, mem_new_big_1_p25
  alu alu_1 (
    .X(register_2_q0), .Y(register_2_q0), .A(undriven), .CLOCK(clk_1_clock_signal), .ALU_EN(cte_cu_1_p8),
    .ALU_CTRL0(cte_cu_1_p9), .ALU_CTRL1(cte_cu_1_p10), .ALU_CTRL2(cte_cu_1_p11),
    .CARRY_FLAG(alu_1_carry_flag), .ZERO_FLAG(alu_1_zero_flag));  // open: CARRY_IN
  LedBar ledbar_9 (
    .led0(register_5_out_12), .led1(register_5_out_13), .led2(register_5_out_14), .led3(register_5_out_15),
    .led4(register_5_out_16), .led5(register_5_out_17), .led6(register_5_out_18), .led7(register_5_dg0));
  LedBar ledbar_10 (
    .led0(register_6_out_12), .led1(register_6_out_13), .led2(register_6_out_14), .led3(register_6_out_15),
    .led4(register_6_out_16), .led5(register_6_out_17), .led6(register_6_out_18), .led7(register_6_dg0));
  LedBar ledbar_11 (
    .led0(register_7_out_12), .led1(register_7_out_13), .led2(register_7_out_14), .led3(register_7_out_15),
    .led4(register_7_out_16), .led5(register_7_out_17), .led6(register_7_out_18), .led7(register_7_dg0));
  LedBar ledbar_12 (
    .led0(register_8_out_12), .led1(register_8_out_13), .led2(register_8_out_14), .led3(register_8_out_15),
    .led4(register_8_out_16), .led5(register_8_out_17), .led6(register_8_out_18), .led7(register_8_dg0));
  LedBar ledbar_13 (
    .led0(register_9_out_12), .led1(register_9_out_13), .led2(register_9_out_14), .led3(register_9_out_15),
    .led4(register_9_out_16), .led5(register_9_out_17), .led6(register_9_out_18), .led7(register_9_dg0));
  register register_5 (
    .en_input(cte_cu_1_p22), .clock(clk_1_clock_signal), .D0(register_2_q0[0]), .D1(register_2_q0[1]),
    .D2(register_2_q0[2]), .D3(register_2_q0[3]), .D4(register_2_q0[4]), .D5(register_2_q0[5]),
    .D6(register_2_q0[6]), .D7(register_2_q0[7]), .en_output(cte_cu_1_p23), .Q0(register_2_q0[0]),
    .Q1(register_2_q0[1]), .Q2(register_2_q0[2]), .Q3(register_2_q0[3]), .Q4(register_2_q0[4]),
    .Q5(register_2_q0[5]), .Q6(register_2_q0[6]), .Q7(register_2_q0[7]), .out_12(register_5_out_12),
    .out_13(register_5_out_13), .out_14(register_5_out_14), .out_15(register_5_out_15),
    .out_16(register_5_out_16), .out_17(register_5_out_17), .out_18(register_5_out_18), .DG0(register_5_dg0));
  register register_6 (
    .en_input(cte_cu_1_p24), .clock(clk_1_clock_signal), .D0(register_2_q0[0]), .D1(register_2_q0[1]),
    .D2(register_2_q0[2]), .D3(register_2_q0[3]), .D4(register_2_q0[4]), .D5(register_2_q0[5]),
    .D6(register_2_q0[6]), .D7(register_2_q0[7]), .en_output(cte_cu_1_p25), .Q0(pc_1_o[0]), .Q1(pc_1_o[1]),
    .Q2(pc_1_o[2]), .Q3(pc_1_o[3]), .Q4(pc_1_o[4]), .Q5(pc_1_o[5]), .Q6(pc_1_o[6]), .Q7(pc_1_o[7]),
    .out_12(register_6_out_12), .out_13(register_6_out_13), .out_14(register_6_out_14),
    .out_15(register_6_out_15), .out_16(register_6_out_16), .out_17(register_6_out_17),
    .out_18(register_6_out_18), .DG0(register_6_dg0));
  register register_7 (
    .en_input(cte_cu_1_p16), .clock(clk_1_clock_signal), .D0(register_2_q0[0]), .D1(register_2_q0[1]),
    .D2(register_2_q0[2]), .D3(register_2_q0[3]), .D4(register_2_q0[4]), .D5(register_2_q0[5]),
    .D6(register_2_q0[6]), .D7(register_2_q0[7]), .en_output(cte_cu_1_p17), .Q0(register_2_q0[0]),
    .Q1(register_2_q0[1]), .Q2(register_2_q0[2]), .Q3(register_2_q0[3]), .Q4(register_2_q0[4]),
    .Q5(register_2_q0[5]), .Q6(register_2_q0[6]), .Q7(register_2_q0[7]), .out_12(register_7_out_12),
    .out_13(register_7_out_13), .out_14(register_7_out_14), .out_15(register_7_out_15),
    .out_16(register_7_out_16), .out_17(register_7_out_17), .out_18(register_7_out_18), .DG0(register_7_dg0));
  register register_8 (
    .D0(alu_1_carry_flag), .D1(alu_1_zero_flag), .Q0(register_8_q0[0]), .Q1(register_8_q0[1]),
    .Q2(register_8_q0[2]), .Q3(register_8_q0[3]), .Q4(register_8_q0[4]), .Q5(register_8_q0[5]),
    .Q6(register_8_q0[6]), .Q7(register_8_q0[7]), .out_12(register_8_out_12), .out_13(register_8_out_13),
    .out_14(register_8_out_14), .out_15(register_8_out_15), .out_16(register_8_out_16),
    .out_17(register_8_out_17), .out_18(register_8_out_18), .DG0(register_8_dg0));  // open: en_input, clock, D2, D3, D4, D5, D6, D7, en_output
  register register_9 (
    .en_input(cte_cu_1_p18), .clock(clk_1_clock_signal), .D0(undriven[0]), .D1(undriven[1]),
    .D2(undriven[2]), .D3(undriven[3]), .D4(undriven[4]), .D5(undriven[5]), .D6(undriven[6]),
    .D7(undriven[7]), .en_output(cte_cu_1_p19), .Q0(register_2_q0[0]), .Q1(register_2_q0[1]),
    .Q2(register_2_q0[2]), .Q3(register_2_q0[3]), .Q4(register_2_q0[4]), .Q5(register_2_q0[5]),
    .Q6(register_2_q0[6]), .Q7(register_2_q0[7]), .out_12(register_9_out_12), .out_13(register_9_out_13),
    .out_14(register_9_out_14), .out_15(register_9_out_15), .out_16(register_9_out_16),
    .out_17(register_9_out_17), .out_18(register_9_out_18), .DG0(register_9_dg0));
  LedBar #(.matrixcols(32)) ledbar_14 (
    .led0(cte_cu_1_p4), .led1(cte_cu_1_p5), .led2(cte_cu_1_p6), .led3(cte_cu_1_p7), .led4(cte_cu_1_p8),
    .led5(cte_cu_1_p9), .led6(cte_cu_1_p10), .led7(cte_cu_1_p11), .led8(mem_new_big_1_p24),
    .led9(mem_new_big_1_p25), .led10(cte_cu_1_p14), .led11(cte_cu_1_p15), .led12(cte_cu_1_p16),
    .led13(cte_cu_1_p17), .led14(cte_cu_1_p18), .led15(cte_cu_1_p19), .led16(mem_new_big_1_p22),
    .led17(cte_cu_1_p21), .led18(cte_cu_1_p22), .led19(cte_cu_1_p23), .led20(cte_cu_1_p24),
    .led21(cte_cu_1_p25), .led22(cte_cu_1_p26), .led23(cte_cu_1_p27), .led24(cte_cu_1_p28),
    .led25(cte_cu_1_p30), .led26(cte_cu_1_p32), .led27(cte_cu_1_p34), .led28(cte_cu_1_p36),
    .led29(cte_cu_1_p38), .led30(cte_cu_1_p40), .led31(cte_cu_1_p42));
  // cte_cu cte_cu_1: pin names not known; wires that end beside it: register_8_q0, register_1_q0, clk_1_clock_signal, cte_cu_1_p4, cte_cu_1_p5, cte_cu_1_p6, cte_cu_1_p7, cte_cu_1_p8, cte_cu_1_p9, cte_cu_1_p10, cte_cu_1_p11, mem_new_big_1_p24, mem_new_big_1_p25, cte_cu_1_p14, cte_cu_1_p15, cte_cu_1_p16, cte_cu_1_p17, cte_cu_1_p18, cte_cu_1_p19, mem_new_big_1_p22, cte_cu_1_p21, cte_cu_1_p22, cte_cu_1_p23, cte_cu_1_p24, cte_cu_1_p25, cte_cu_1_p26, cte_cu_1_p27, cte_cu_1_p28, cte_cu_1_p29, cte_cu_1_p30, cte_cu_1_p31, cte_cu_1_p32, cte_cu_1_p33, cte_cu_1_p34, cte_cu_1_p35, cte_cu_1_p36, cte_cu_1_p37, cte_cu_1_p38, cte_cu_1_p39, cte_cu_1_p40, cte_cu_1_p41, cte_cu_1_p42, cte_cu_1_p43
  LedBar #(.matrixcols(1)) ledbar_15 ();  // open: led0
  LedBar ledbar_16 (
    .led0(cte_cu_1_p29), .led1(cte_cu_1_p31), .led2(cte_cu_1_p33), .led3(cte_cu_1_p35), .led4(cte_cu_1_p37),
    .led5(cte_cu_1_p39), .led6(cte_cu_1_p41), .led7(cte_cu_1_p43));

  // Notes on the sheet:
  //   ADDRESS BUS
  //   CLOCK
  //   DATA BUS
  //   7
  //   4
  //   INSTRUCTION REGISTER
  //   8
  //   1
  //   5
  //   6
  //   2
  //   3
  //   CONTROL BUS
endmodule

module Counter_8_bits (
  input  COut,
  input  CEnable,
  input  CWrite,
  input  CReset,
  input  Clock,
  input  I7,
  input  in_7,
  input  in_8,
  input  in_9,
  input  in_10,
  input  in_11,
  input  in_12,
  input  I0,
  output O7,
  output out_15,
  output out_16,
  output out_17,
  output out_18,
  output out_19,
  output out_20,
  output O0
);

  wire and_1_out, and_2_out, and_3_out, and_4_out, and_5_out, and_6_out, and_7_out, and_8_out, and_9_out,
       and_10_out, and_11_out, and_12_out, and_13_out, and_14_out, and_15_out, and_16_out, j_k_ff_1_q,
       j_k_ff_2_q, j_k_ff_2_qn, j_k_ff_3_q, j_k_ff_3_qn, j_k_ff_4_q, j_k_ff_4_qn, j_k_ff_5_q, j_k_ff_5_qn,
       j_k_ff_6_q, j_k_ff_6_qn, j_k_ff_7_q, j_k_ff_7_qn, j_k_ff_8_q, j_k_ff_8_qn, or_1_out, or_2_out,
       or_3_out, or_4_out, or_5_out, or_6_out, or_7_out, or_8_out;

  assign O7 = COut ? j_k_ff_1_q : 1'bz;  // Controlled_Buffer controlled_buffer_1
  J_K_Flip_Flop j_k_ff_1 (
    .J(CEnable), .K(CEnable), .clk(j_k_ff_2_qn), .Q(j_k_ff_1_q), .preset(and_1_out), .reset(or_1_out));  // open: Qn
  or or_1 (or_1_out, CReset, and_2_out);
  and and_1 (and_1_out, CWrite, I7, Clock);
  and and_2 (and_2_out, CWrite, ~I7, Clock);  // AND_Gate
  J_K_Flip_Flop j_k_ff_2 (
    .J(CEnable), .K(CEnable), .clk(j_k_ff_3_qn), .Q(j_k_ff_2_q), .Qn(j_k_ff_2_qn), .preset(and_3_out),
    .reset(or_2_out));
  or or_2 (or_2_out, CReset, and_4_out);
  and and_3 (and_3_out, CWrite, in_7, Clock);
  and and_4 (and_4_out, CWrite, ~in_7, Clock);  // AND_Gate
  assign out_15 = COut ? j_k_ff_2_q : 1'bz;  // Controlled_Buffer controlled_buffer_2
  J_K_Flip_Flop j_k_ff_3 (
    .J(CEnable), .K(CEnable), .clk(j_k_ff_4_qn), .Q(j_k_ff_3_q), .Qn(j_k_ff_3_qn), .preset(and_5_out),
    .reset(or_3_out));
  or or_3 (or_3_out, CReset, and_6_out);
  and and_5 (and_5_out, CWrite, in_8, Clock);
  assign out_16 = COut ? j_k_ff_3_q : 1'bz;  // Controlled_Buffer controlled_buffer_3
  J_K_Flip_Flop j_k_ff_4 (
    .J(CEnable), .K(CEnable), .clk(j_k_ff_5_qn), .Q(j_k_ff_4_q), .Qn(j_k_ff_4_qn), .preset(and_7_out),
    .reset(or_4_out));
  and and_6 (and_6_out, CWrite, ~in_8, Clock);  // AND_Gate
  and and_7 (and_7_out, CWrite, in_9, Clock);
  assign out_17 = COut ? j_k_ff_4_q : 1'bz;  // Controlled_Buffer controlled_buffer_4
  or or_4 (or_4_out, CReset, and_8_out);
  and and_8 (and_8_out, CWrite, ~in_9, Clock);  // AND_Gate
  assign out_18 = COut ? j_k_ff_5_q : 1'bz;  // Controlled_Buffer controlled_buffer_5
  J_K_Flip_Flop j_k_ff_5 (
    .J(CEnable), .K(CEnable), .clk(j_k_ff_6_qn), .Q(j_k_ff_5_q), .Qn(j_k_ff_5_qn), .preset(and_9_out),
    .reset(or_5_out));
  or or_5 (or_5_out, CReset, and_10_out);
  and and_9 (and_9_out, CWrite, in_10, Clock);
  and and_10 (and_10_out, CWrite, ~in_10, Clock);  // AND_Gate
  J_K_Flip_Flop j_k_ff_6 (
    .J(CEnable), .K(CEnable), .clk(j_k_ff_7_qn), .Q(j_k_ff_6_q), .Qn(j_k_ff_6_qn), .preset(and_11_out),
    .reset(or_6_out));
  or or_6 (or_6_out, CReset, and_12_out);
  and and_11 (and_11_out, CWrite, in_11, Clock);
  and and_12 (and_12_out, CWrite, ~in_11, Clock);  // AND_Gate
  assign out_19 = COut ? j_k_ff_6_q : 1'bz;  // Controlled_Buffer controlled_buffer_6
  J_K_Flip_Flop j_k_ff_7 (
    .J(CEnable), .K(CEnable), .clk(j_k_ff_8_qn), .Q(j_k_ff_7_q), .Qn(j_k_ff_7_qn), .preset(and_13_out),
    .reset(or_7_out));
  or or_7 (or_7_out, CReset, and_15_out);
  and and_13 (and_13_out, CWrite, in_12, Clock);
  assign out_20 = COut ? j_k_ff_7_q : 1'bz;  // Controlled_Buffer controlled_buffer_7
  J_K_Flip_Flop j_k_ff_8 (
    .J(CEnable), .K(CEnable), .clk(Clock), .Q(j_k_ff_8_q), .Qn(j_k_ff_8_qn), .preset(and_14_out),
    .reset(or_8_out));
  and and_14 (and_14_out, CWrite, I0, Clock);
  and and_15 (and_15_out, CWrite, ~in_12, Clock);  // AND_Gate
  assign O0 = COut ? j_k_ff_8_q : 1'bz;  // Controlled_Buffer controlled_buffer_8
  or or_8 (or_8_out, CReset, and_16_out);
  and and_16 (and_16_out, CWrite, ~I0, Clock);  // AND_Gate
endmodule

module memory_new_small (
  input  clock,
  input  read,
  input  write,
  input  D7,
  input  in_5,
  input  in_6,
  input  in_7,
  input  in_8,
  input  in_9,
  input  in_10,
  input  D0,
  input  A3,
  input  in_13,
  input  in_14,
  input  A0,
  output Q7,
  output out_17,
  output out_18,
  output out_19,
  output out_20,
  output out_21,
  output out_22,
  output Q0
);

  wire and_1_out, and_2_out, and_3_out, and_4_out, and_5_out, and_6_out, and_7_out, and_8_out, and_9_out,
       and_10_out, and_11_out, and_12_out, and_13_out, and_14_out, and_15_out, and_16_out, and_17_out,
       and_18_out, and_19_out, and_20_out, and_21_out, and_22_out, and_23_out, and_24_out, and_25_out,
       and_26_out, and_27_out, and_28_out, and_29_out, and_30_out, and_31_out, and_32_out, R, R_1, R_2, R_3,
       R_4, R_5, R_6, R_7, R_8, R_9, R_10, R_11, R_12, R_13, R_14, R_15;

  decoder decoder_1 (
    .D0(A0), .in_2(in_14), .in_3(in_13), .in_4(A3), .out_5(R_15), .out_6(R_14), .out_7(R_13), .out_8(R_12),
    .out_9(R_11), .out_10(R_10), .out_11(R_9), .out_12(R_8), .out_13(R_7), .out_14(R_6), .out_15(R_5),
    .out_16(R_4), .out_17(R_3), .out_18(R_2), .out_19(R_1), .out_20(R));
  register register_1 (
    .en_input(and_1_out), .clock(clock), .D0(D0), .D1(in_10), .D2(in_9), .D3(in_8), .D4(in_7), .D5(in_6),
    .D6(in_5), .D7(D7), .en_output(and_2_out), .Q0(Q0), .Q1(out_22), .Q2(out_21), .Q3(out_20), .Q4(out_19),
    .Q5(out_18), .Q6(out_17), .Q7(Q7));  // open: out_12, out_13, out_14, out_15, out_16, out_17, out_18, DG0
  register register_2 (
    .en_input(and_3_out), .clock(clock), .D0(D0), .D1(in_10), .D2(in_9), .D3(in_8), .D4(in_7), .D5(in_6),
    .D6(in_5), .D7(D7), .en_output(and_4_out), .Q0(Q0), .Q1(out_22), .Q2(out_21), .Q3(out_20), .Q4(out_19),
    .Q5(out_18), .Q6(out_17), .Q7(Q7));  // open: out_12, out_13, out_14, out_15, out_16, out_17, out_18, DG0
  register register_3 (
    .en_input(and_5_out), .clock(clock), .D0(D0), .D1(in_10), .D2(in_9), .D3(in_8), .D4(in_7), .D5(in_6),
    .D6(in_5), .D7(D7), .en_output(and_6_out), .Q0(Q0), .Q1(out_22), .Q2(out_21), .Q3(out_20), .Q4(out_19),
    .Q5(out_18), .Q6(out_17), .Q7(Q7));  // open: out_12, out_13, out_14, out_15, out_16, out_17, out_18, DG0
  register register_4 (
    .en_input(and_7_out), .clock(clock), .D0(D0), .D1(in_10), .D2(in_9), .D3(in_8), .D4(in_7), .D5(in_6),
    .D6(in_5), .D7(D7), .en_output(and_8_out), .Q0(Q0), .Q1(out_22), .Q2(out_21), .Q3(out_20), .Q4(out_19),
    .Q5(out_18), .Q6(out_17), .Q7(Q7));  // open: out_12, out_13, out_14, out_15, out_16, out_17, out_18, DG0
  and and_1 (and_1_out, write, R);
  and and_2 (and_2_out, R, read);
  and and_3 (and_3_out, write, R_4);
  and and_4 (and_4_out, R_4, read);
  and and_5 (and_5_out, write, R_8);
  and and_6 (and_6_out, R_8, read);
  and and_7 (and_7_out, write, R_12);
  and and_8 (and_8_out, R_12, read);
  and and_9 (and_9_out, write, R_1);
  and and_10 (and_10_out, R_1, read);
  register register_5 (
    .en_input(and_9_out), .clock(clock), .D0(D0), .D1(in_10), .D2(in_9), .D3(in_8), .D4(in_7), .D5(in_6),
    .D6(in_5), .D7(D7), .en_output(and_10_out), .Q0(Q0), .Q1(out_22), .Q2(out_21), .Q3(out_20), .Q4(out_19),
    .Q5(out_18), .Q6(out_17), .Q7(Q7));  // open: out_12, out_13, out_14, out_15, out_16, out_17, out_18, DG0
  and and_11 (and_11_out, write, R_5);
  and and_12 (and_12_out, R_5, read);
  register register_6 (
    .en_input(and_11_out), .clock(clock), .D0(D0), .D1(in_10), .D2(in_9), .D3(in_8), .D4(in_7), .D5(in_6),
    .D6(in_5), .D7(D7), .en_output(and_12_out), .Q0(Q0), .Q1(out_22), .Q2(out_21), .Q3(out_20), .Q4(out_19),
    .Q5(out_18), .Q6(out_17), .Q7(Q7));  // open: out_12, out_13, out_14, out_15, out_16, out_17, out_18, DG0
  and and_13 (and_13_out, write, R_9);
  and and_14 (and_14_out, R_9, read);
  register register_7 (
    .en_input(and_13_out), .clock(clock), .D0(D0), .D1(in_10), .D2(in_9), .D3(in_8), .D4(in_7), .D5(in_6),
    .D6(in_5), .D7(D7), .en_output(and_14_out), .Q0(Q0), .Q1(out_22), .Q2(out_21), .Q3(out_20), .Q4(out_19),
    .Q5(out_18), .Q6(out_17), .Q7(Q7));  // open: out_12, out_13, out_14, out_15, out_16, out_17, out_18, DG0
  and and_15 (and_15_out, write, R_13);
  and and_16 (and_16_out, R_13, read);
  register register_8 (
    .en_input(and_15_out), .clock(clock), .D0(D0), .D1(in_10), .D2(in_9), .D3(in_8), .D4(in_7), .D5(in_6),
    .D6(in_5), .D7(D7), .en_output(and_16_out), .Q0(Q0), .Q1(out_22), .Q2(out_21), .Q3(out_20), .Q4(out_19),
    .Q5(out_18), .Q6(out_17), .Q7(Q7));  // open: out_12, out_13, out_14, out_15, out_16, out_17, out_18, DG0
  register register_9 (
    .en_input(and_17_out), .clock(clock), .D0(D0), .D1(in_10), .D2(in_9), .D3(in_8), .D4(in_7), .D5(in_6),
    .D6(in_5), .D7(D7), .en_output(and_18_out), .Q0(Q0), .Q1(out_22), .Q2(out_21), .Q3(out_20), .Q4(out_19),
    .Q5(out_18), .Q6(out_17), .Q7(Q7));  // open: out_12, out_13, out_14, out_15, out_16, out_17, out_18, DG0
  register register_10 (
    .en_input(and_19_out), .clock(clock), .D0(D0), .D1(in_10), .D2(in_9), .D3(in_8), .D4(in_7), .D5(in_6),
    .D6(in_5), .D7(D7), .en_output(and_20_out), .Q0(Q0), .Q1(out_22), .Q2(out_21), .Q3(out_20), .Q4(out_19),
    .Q5(out_18), .Q6(out_17), .Q7(Q7));  // open: out_12, out_13, out_14, out_15, out_16, out_17, out_18, DG0
  register register_11 (
    .en_input(and_21_out), .clock(clock), .D0(D0), .D1(in_10), .D2(in_9), .D3(in_8), .D4(in_7), .D5(in_6),
    .D6(in_5), .D7(D7), .en_output(and_22_out), .Q0(Q0), .Q1(out_22), .Q2(out_21), .Q3(out_20), .Q4(out_19),
    .Q5(out_18), .Q6(out_17), .Q7(Q7));  // open: out_12, out_13, out_14, out_15, out_16, out_17, out_18, DG0
  register register_12 (
    .en_input(and_23_out), .clock(clock), .D0(D0), .D1(in_10), .D2(in_9), .D3(in_8), .D4(in_7), .D5(in_6),
    .D6(in_5), .D7(D7), .en_output(and_24_out), .Q0(Q0), .Q1(out_22), .Q2(out_21), .Q3(out_20), .Q4(out_19),
    .Q5(out_18), .Q6(out_17), .Q7(Q7));  // open: out_12, out_13, out_14, out_15, out_16, out_17, out_18, DG0
  and and_17 (and_17_out, write, R_2);
  and and_18 (and_18_out, R_2, read);
  and and_19 (and_19_out, write, R_6);
  and and_20 (and_20_out, R_6, read);
  and and_21 (and_21_out, write, R_10);
  and and_22 (and_22_out, R_10, read);
  and and_23 (and_23_out, write, R_14);
  and and_24 (and_24_out, R_14, read);
  and and_25 (and_25_out, write, R_3);
  and and_26 (and_26_out, R_3, read);
  register register_13 (
    .en_input(and_25_out), .clock(clock), .D0(D0), .D1(in_10), .D2(in_9), .D3(in_8), .D4(in_7), .D5(in_6),
    .D6(in_5), .D7(D7), .en_output(and_26_out), .Q0(Q0), .Q1(out_22), .Q2(out_21), .Q3(out_20), .Q4(out_19),
    .Q5(out_18), .Q6(out_17), .Q7(Q7));  // open: out_12, out_13, out_14, out_15, out_16, out_17, out_18, DG0
  and and_27 (and_27_out, write, R_7);
  and and_28 (and_28_out, R_7, read);
  register register_14 (
    .en_input(and_27_out), .clock(clock), .D0(D0), .D1(in_10), .D2(in_9), .D3(in_8), .D4(in_7), .D5(in_6),
    .D6(in_5), .D7(D7), .en_output(and_28_out), .Q0(Q0), .Q1(out_22), .Q2(out_21), .Q3(out_20), .Q4(out_19),
    .Q5(out_18), .Q6(out_17), .Q7(Q7));  // open: out_12, out_13, out_14, out_15, out_16, out_17, out_18, DG0
  and and_29 (and_29_out, write, R_11);
  and and_30 (and_30_out, R_11, read);
  register register_15 (
    .en_input(and_29_out), .clock(clock), .D0(D0), .D1(in_10), .D2(in_9), .D3(in_8), .D4(in_7), .D5(in_6),
    .D6(in_5), .D7(D7), .en_output(and_30_out), .Q0(Q0), .Q1(out_22), .Q2(out_21), .Q3(out_20), .Q4(out_19),
    .Q5(out_18), .Q6(out_17), .Q7(Q7));  // open: out_12, out_13, out_14, out_15, out_16, out_17, out_18, DG0
  and and_31 (and_31_out, write, R_15);
  and and_32 (and_32_out, R_15, read);
  register register_16 (
    .en_input(and_31_out), .clock(clock), .D0(D0), .D1(in_10), .D2(in_9), .D3(in_8), .D4(in_7), .D5(in_6),
    .D6(in_5), .D7(D7), .en_output(and_32_out), .Q0(Q0), .Q1(out_22), .Q2(out_21), .Q3(out_20), .Q4(out_19),
    .Q5(out_18), .Q6(out_17), .Q7(Q7));  // open: out_12, out_13, out_14, out_15, out_16, out_17, out_18, DG0

  // Other names for the same wires on the sheet: D[6:1] = {in_5, in_6, in_7, in_8, in_9, in_10};
  //   Q[6:1] = {out_17, out_18, out_19, out_20, out_21, out_22}
endmodule

module mem_new_big (
  input  clock,
  input  read,
  input  write,
  input  D7,
  input  in_5,
  input  in_6,
  input  in_7,
  input  in_8,
  input  in_9,
  input  in_10,
  input  D0,
  input  A3,
  input  in_13,
  input  in_14,
  input  A0,
  input  A7,
  input  in_17,
  input  in_18,
  input  A5,
  output Q7,
  output out_21,
  output out_22,
  output out_23,
  output out_24,
  output out_25,
  output out_26,
  output Q0
);

  wire and_1_out, and_2_out, and_3_out, and_4_out, and_5_out, and_6_out, and_7_out, and_8_out, and_9_out,
       and_10_out, and_11_out, and_12_out, and_13_out, and_14_out, and_15_out, and_16_out, and_17_out,
       and_18_out, and_19_out, and_20_out, and_21_out, and_22_out, and_23_out, and_24_out, and_25_out,
       and_26_out, and_27_out, and_28_out, and_29_out, and_30_out, and_31_out, and_32_out,
       memory_new_small_1_p1, memory_new_small_2_p1, memory_new_small_3_p1, memory_new_small_4_p1, R, R_1,
       R_2, R_3, R_4, R_5, R_6, R_7, R_8, R_9, R_10, R_11, R_12, R_13, R_14, R_15;

  decoder decoder_1 (
    .D0(A5), .in_2(in_18), .in_3(in_17), .in_4(A7), .out_5(R_15), .out_6(R_14), .out_7(R_13), .out_8(R_12),
    .out_9(R_11), .out_10(R_10), .out_11(R_9), .out_12(R_8), .out_13(R_7), .out_14(R_6), .out_15(R_5),
    .out_16(R_4), .out_17(R_3), .out_18(R_2), .out_19(R_1), .out_20(R));
  // memory_new_small memory_new_small_1: pin names not known; wires that end beside it: memory_new_small_1_p1, memory_new_small_1_p1, D0, in_10, in_9, in_8, in_7, in_6, in_5
  // memory_new_small memory_new_small_2: pin names not known; wires that end beside it: memory_new_small_2_p1, memory_new_small_2_p1, D0, in_10, in_9, in_8, in_7, in_6, in_5
  // memory_new_small memory_new_small_3: pin names not known; wires that end beside it: memory_new_small_3_p1, memory_new_small_3_p1, D0, in_10, in_9, in_8, in_7, in_6, in_5
  // memory_new_small memory_new_small_4: pin names not known; wires that end beside it: memory_new_small_4_p1, memory_new_small_4_p1, D0, in_10, in_9, in_8, in_7, in_6, in_5
  and and_1 (and_1_out, write, R);
  and and_2 (and_2_out, R, read);
  and and_3 (and_3_out, write, R_4);
  and and_4 (and_4_out, R_4, read);
  and and_5 (and_5_out, write, R_8);
  and and_6 (and_6_out, R_8, read);
  and and_7 (and_7_out, write, R_12);
  and and_8 (and_8_out, R_12, read);
  // memory_new_small memory_new_small_5: pin names not known; wires that end beside it: write, R, read, D0, in_10, in_9, in_8, in_7, in_6, in_5
  // memory_new_small memory_new_small_6: pin names not known; wires that end beside it: write, R_4, read, D0, in_10, in_9, in_8, in_7, in_6, in_5
  // memory_new_small memory_new_small_7: pin names not known; wires that end beside it: write, R_8, read, D0, in_10, in_9, in_8, in_7, in_6, in_5
  // memory_new_small memory_new_small_8: pin names not known; wires that end beside it: write, R_12, read, D0, in_10, in_9, in_8, in_7, in_6, in_5
  and and_9 (and_9_out, write, R_1);
  and and_10 (and_10_out, R_1, read);
  and and_11 (and_11_out, write, R_5);
  and and_12 (and_12_out, R_5, read);
  and and_13 (and_13_out, write, R_9);
  and and_14 (and_14_out, R_9, read);
  and and_15 (and_15_out, write, R_13);
  and and_16 (and_16_out, R_13, read);
  // memory_new_small memory_new_small_9: pin names not known; wires that end beside it: write, R_1, read, D0, in_10, in_9, in_8, in_7, in_6, in_5
  // memory_new_small memory_new_small_10: pin names not known; wires that end beside it: write, R_5, read, D0, in_10, in_9, in_8, in_7, in_6, in_5
  // memory_new_small memory_new_small_11: pin names not known; wires that end beside it: write, R_9, read, D0, in_10, in_9, in_8, in_7, in_6, in_5
  // memory_new_small memory_new_small_12: pin names not known; wires that end beside it: write, R_13, read, D0, in_10, in_9, in_8, in_7, in_6, in_5
  and and_17 (and_17_out, write, R_2);
  and and_18 (and_18_out, R_2, read);
  and and_19 (and_19_out, write, R_6);
  and and_20 (and_20_out, R_6, read);
  and and_21 (and_21_out, write, R_10);
  and and_22 (and_22_out, R_10, read);
  and and_23 (and_23_out, write, R_14);
  and and_24 (and_24_out, R_14, read);
  // memory_new_small memory_new_small_13: pin names not known; wires that end beside it: write, R_2, read, D0, in_10, in_9, in_8, in_7, in_6, in_5
  // memory_new_small memory_new_small_14: pin names not known; wires that end beside it: write, R_6, read, D0, in_10, in_9, in_8, in_7, in_6, in_5
  // memory_new_small memory_new_small_15: pin names not known; wires that end beside it: write, R_10, read, D0, in_10, in_9, in_8, in_7, in_6, in_5
  // memory_new_small memory_new_small_16: pin names not known; wires that end beside it: write, R_14, read, D0, in_10, in_9, in_8, in_7, in_6, in_5
  and and_25 (and_25_out, write, R_3);
  and and_26 (and_26_out, R_3, read);
  and and_27 (and_27_out, write, R_7);
  and and_28 (and_28_out, R_7, read);
  and and_29 (and_29_out, write, R_11);
  and and_30 (and_30_out, R_11, read);
  and and_31 (and_31_out, write, R_15);
  and and_32 (and_32_out, R_15, read);

  // Other names for the same wires on the sheet: addr[3:0] = {A3, in_13, in_14, A0};
  //   D[6:1] = {in_5, in_6, in_7, in_8, in_9, in_10}; Q[6:1] = {out_21, out_22, out_23, out_24, out_25, out_26}
endmodule

module alu (
  input  [7:0] X,
  input  [7:0] Y,
  input  CARRY_IN,
  input  [7:0] A,
  input  CLOCK,
  input  ALU_EN,
  input  ALU_CTRL0,
  input  ALU_CTRL1,
  input  ALU_CTRL2,
  output CARRY_FLAG,
  output ZERO_FLAG
);

  wire B_OR_SUB0, B_OR_SUB1, B_OR_SUB2, B_OR_SUB3, B_OR_SUB4, B_OR_SUB5, B_OR_SUB6, B_OR_SUB7,
       bus_transceiver_1_q0, bus_transceiver_1_q1, bus_transceiver_1_q2, bus_transceiver_1_q3,
       bus_transceiver_1_q4, bus_transceiver_1_q5, bus_transceiver_1_q6, bus_transceiver_1_q7, CALC,
       Cin_OR_SUB, n7404_2_pin2, n7404_2_pin8, n7404_2_pin10, n7404_2_pin12, n7404_3_pin2, n7404_3_pin8,
       n7404_3_pin10, n7404_3_pin12, n7408_1_pin3, n7408_1_pin6, n7408_1_pin8, n7408_1_pin11, n7408_2_pin3,
       n7408_2_pin6, n7408_2_pin8, n7408_2_pin11, n7408_3_pin3, n7408_3_pin6, n7408_3_pin8, n7408_3_pin11,
       n7408_4_pin3, n7408_4_pin6, n7408_4_pin8, n7408_4_pin11, n7408_5_pin3, n7408_5_pin6, n7408_5_pin8,
       n7408_5_pin11, n7408_6_pin3, n7408_6_pin6, n7408_6_pin8, n7408_6_pin11, n7432_1_pin3, n7432_1_pin6,
       n7432_1_pin8, n7432_1_pin11, n7432_2_pin3, n7432_2_pin6, n7432_2_pin8, n7432_2_pin11, n7432_6_pin11,
       n7486_3_pin1, n7486_3_pin2, n7486_3_pin3, n7486_3_pin5, n7486_3_pin6, n7486_4_pin3, n7486_4_pin6,
       n7486_4_pin8, n7486_4_pin11, n7486_5_pin3, n7486_5_pin6, n7486_5_pin8, n7486_5_pin11, n7486_6_pin1,
       n7486_6_pin2, n7486_6_pin3, n7486_6_pin4, n7486_6_pin5, n7486_6_pin6, n7486_7_pin1, n7486_7_pin2,
       n7486_7_pin3, n7486_7_pin4, n7486_7_pin5, n7486_7_pin6, n7486_8_pin1, n7486_8_pin2, n7486_8_pin3,
       n7486_8_pin4, n7486_8_pin5, n7486_8_pin6, nor_1_out, nor_2_out, NotCtrl0, NotCtrl1, NotCtrl2, S_ADD,
       S_AND, S_NOT, S_OR, S_SUB, S_XOR, xor_2_out;

  _7404 u_7404_1 (
    .pin13(ALU_CTRL2), .pin12(NotCtrl2), .pin11(ALU_CTRL1), .pin10(NotCtrl1), .pin9(ALU_CTRL0),
    .pin8(NotCtrl0));  // open: pin1, pin2, pin3, pin4, pin5, pin6
  _7411 u_7411_1 (
    .pin1(NotCtrl1), .pin2(NotCtrl2), .pin3(NotCtrl0), .pin4(ALU_CTRL1), .pin5(NotCtrl2), .pin6(S_AND),
    .pin13(ALU_CTRL0), .pin12(S_SUB), .pin11(NotCtrl2), .pin10(NotCtrl1), .pin9(NotCtrl0), .pin8(S_ADD));
  _7411 u_7411_2 (
    .pin1(NotCtrl1), .pin2(ALU_CTRL2), .pin3(ALU_CTRL0), .pin4(NotCtrl1), .pin5(ALU_CTRL2), .pin6(S_NOT),
    .pin13(NotCtrl0), .pin12(S_XOR), .pin11(NotCtrl2), .pin10(ALU_CTRL1), .pin9(ALU_CTRL0), .pin8(S_OR));
  _7486 u_7486_1 (
    .pin1(S_SUB), .pin2(Y[3]), .pin3(B_OR_SUB3), .pin4(S_SUB), .pin5(Y[2]), .pin6(B_OR_SUB2), .pin13(S_SUB),
    .pin12(Y[1]), .pin11(B_OR_SUB1), .pin10(S_SUB), .pin9(Y[0]), .pin8(B_OR_SUB0));
  _7486 u_7486_2 (
    .pin1(S_SUB), .pin2(Y[7]), .pin3(B_OR_SUB7), .pin4(S_SUB), .pin5(Y[6]), .pin6(B_OR_SUB6), .pin13(S_SUB),
    .pin12(Y[5]), .pin11(B_OR_SUB5), .pin10(S_SUB), .pin9(Y[4]), .pin8(B_OR_SUB4));
  or or_1 (CALC, S_ADD, S_SUB);
  xor xor_1 (Cin_OR_SUB, S_SUB, CARRY_IN);
  _7486 u_7486_3 (
    .pin1(n7486_3_pin1), .pin2(n7486_3_pin2), .pin3(n7486_3_pin3), .pin4(Cin_OR_SUB), .pin5(n7486_3_pin5),
    .pin6(n7486_3_pin6), .pin13(B_OR_SUB1), .pin12(X[1]), .pin11(n7486_3_pin1), .pin10(B_OR_SUB0),
    .pin9(X[0]), .pin8(n7486_3_pin5));
  _7408 u_7408_1 (
    .pin1(X[2]), .pin2(Y[2]), .pin3(n7408_1_pin3), .pin4(X[3]), .pin5(Y[3]), .pin6(n7408_1_pin6),
    .pin13(Y[1]), .pin12(X[1]), .pin11(n7408_1_pin11), .pin10(Y[0]), .pin9(X[0]), .pin8(n7408_1_pin8));
  _7408 u_7408_2 (
    .pin1(X[6]), .pin2(Y[6]), .pin3(n7408_2_pin3), .pin4(X[7]), .pin5(Y[7]), .pin6(n7408_2_pin6),
    .pin13(Y[5]), .pin12(X[5]), .pin11(n7408_2_pin11), .pin10(Y[4]), .pin9(X[4]), .pin8(n7408_2_pin8));
  _7432 u_7432_1 (
    .pin1(X[3]), .pin2(Y[3]), .pin3(n7432_1_pin3), .pin4(X[2]), .pin5(Y[2]), .pin6(n7432_1_pin6),
    .pin13(Y[1]), .pin12(X[1]), .pin11(n7432_1_pin11), .pin10(Y[0]), .pin9(X[0]), .pin8(n7432_1_pin8));
  _7432 u_7432_2 (
    .pin1(X[7]), .pin2(Y[7]), .pin3(n7432_2_pin3), .pin4(X[6]), .pin5(Y[6]), .pin6(n7432_2_pin6),
    .pin13(Y[5]), .pin12(X[5]), .pin11(n7432_2_pin11), .pin10(Y[4]), .pin9(X[4]), .pin8(n7432_2_pin8));
  _7486 u_7486_4 (
    .pin1(X[3]), .pin2(Y[3]), .pin3(n7486_4_pin3), .pin4(X[2]), .pin5(Y[2]), .pin6(n7486_4_pin6),
    .pin13(Y[1]), .pin12(X[1]), .pin11(n7486_4_pin11), .pin10(Y[0]), .pin9(X[0]), .pin8(n7486_4_pin8));
  _7486 u_7486_5 (
    .pin1(X[7]), .pin2(Y[7]), .pin3(n7486_5_pin3), .pin4(X[6]), .pin5(Y[6]), .pin6(n7486_5_pin6),
    .pin13(Y[5]), .pin12(X[5]), .pin11(n7486_5_pin11), .pin10(Y[4]), .pin9(X[4]), .pin8(n7486_5_pin8));
  _7404 u_7404_2 (
    .pin1(X[3]), .pin2(n7404_2_pin2), .pin13(X[2]), .pin12(n7404_2_pin12), .pin11(X[1]),
    .pin10(n7404_2_pin10), .pin9(X[0]), .pin8(n7404_2_pin8));  // open: pin3, pin4, pin5, pin6
  _7404 u_7404_3 (
    .pin1(X[7]), .pin2(n7404_3_pin2), .pin13(X[6]), .pin12(n7404_3_pin12), .pin11(X[5]),
    .pin10(n7404_3_pin10), .pin9(X[4]), .pin8(n7404_3_pin8));  // open: pin3, pin4, pin5, pin6
  _7486 u_7486_6 (
    .pin1(n7486_6_pin1), .pin2(n7486_6_pin2), .pin3(n7486_6_pin3), .pin4(n7486_6_pin4), .pin5(n7486_6_pin5),
    .pin6(n7486_6_pin6), .pin13(B_OR_SUB3), .pin12(X[3]), .pin11(n7486_6_pin1), .pin10(B_OR_SUB2),
    .pin9(X[2]), .pin8(n7486_6_pin5));
  _7486 u_7486_7 (
    .pin1(n7486_7_pin1), .pin2(n7486_7_pin2), .pin3(n7486_7_pin3), .pin4(n7486_7_pin4), .pin5(n7486_7_pin5),
    .pin6(n7486_7_pin6), .pin13(B_OR_SUB5), .pin12(X[5]), .pin11(n7486_7_pin1), .pin10(B_OR_SUB4),
    .pin9(X[4]), .pin8(n7486_7_pin5));
  _7486 u_7486_8 (
    .pin1(n7486_8_pin1), .pin2(n7486_8_pin2), .pin3(n7486_8_pin3), .pin4(n7486_8_pin4), .pin5(n7486_8_pin5),
    .pin6(n7486_8_pin6), .pin13(B_OR_SUB7), .pin12(X[7]), .pin11(n7486_8_pin1), .pin10(B_OR_SUB6),
    .pin9(X[6]), .pin8(n7486_8_pin5));
  bus_transceiver bus_transceiver_1 (
    .D0(n7408_1_pin8), .D1(n7408_1_pin11), .D2(n7408_1_pin3), .D3(n7408_1_pin6), .D4(n7408_2_pin8),
    .D5(n7408_2_pin11), .D6(n7408_2_pin3), .D7(n7408_2_pin6), .BUS_ENABLE(S_AND), .Q0(bus_transceiver_1_q0),
    .Q1(bus_transceiver_1_q1), .Q2(bus_transceiver_1_q2), .Q3(bus_transceiver_1_q3),
    .Q4(bus_transceiver_1_q4), .Q5(bus_transceiver_1_q5), .Q6(bus_transceiver_1_q6), .Q7(bus_transceiver_1_q7));
  bus_transceiver bus_transceiver_2 (
    .D0(n7432_1_pin8), .D1(n7432_1_pin11), .D2(n7432_1_pin6), .D3(n7432_1_pin3), .D4(n7432_2_pin8),
    .D5(n7432_2_pin11), .D6(n7432_2_pin6), .D7(n7432_2_pin3), .BUS_ENABLE(S_OR), .Q0(bus_transceiver_1_q0),
    .Q1(bus_transceiver_1_q1), .Q2(bus_transceiver_1_q2), .Q3(bus_transceiver_1_q3),
    .Q4(bus_transceiver_1_q4), .Q5(bus_transceiver_1_q5), .Q6(bus_transceiver_1_q6), .Q7(bus_transceiver_1_q7));
  _7408 u_7408_3 (
    .pin1(n7486_3_pin1), .pin2(n7486_3_pin2), .pin3(n7408_3_pin3), .pin4(n7486_3_pin5), .pin5(Cin_OR_SUB),
    .pin6(n7408_3_pin6), .pin13(X[1]), .pin12(B_OR_SUB1), .pin11(n7408_3_pin11), .pin10(X[0]),
    .pin9(B_OR_SUB0), .pin8(n7408_3_pin8));
  _7408 u_7408_4 (
    .pin1(n7486_6_pin1), .pin2(n7486_6_pin2), .pin3(n7408_4_pin3), .pin4(n7486_6_pin5), .pin5(n7486_6_pin4),
    .pin6(n7408_4_pin6), .pin13(X[3]), .pin12(B_OR_SUB3), .pin11(n7408_4_pin11), .pin10(X[2]),
    .pin9(B_OR_SUB2), .pin8(n7408_4_pin8));
  _7408 u_7408_5 (
    .pin1(n7486_7_pin1), .pin2(n7486_7_pin2), .pin3(n7408_5_pin3), .pin4(n7486_7_pin5), .pin5(n7486_7_pin4),
    .pin6(n7408_5_pin6), .pin13(X[5]), .pin12(B_OR_SUB5), .pin11(n7408_5_pin11), .pin10(X[4]),
    .pin9(B_OR_SUB4), .pin8(n7408_5_pin8));
  _7408 u_7408_6 (
    .pin1(n7486_8_pin1), .pin2(n7486_8_pin2), .pin3(n7408_6_pin3), .pin4(n7486_8_pin5), .pin5(n7486_8_pin4),
    .pin6(n7408_6_pin6), .pin13(X[7]), .pin12(B_OR_SUB7), .pin11(n7408_6_pin11), .pin10(X[6]),
    .pin9(B_OR_SUB6), .pin8(n7408_6_pin8));
  _7432 u_7432_3 (
    .pin13(n7408_3_pin11), .pin12(n7408_3_pin3), .pin11(n7486_6_pin4), .pin10(n7408_3_pin6),
    .pin9(n7408_3_pin8), .pin8(n7486_3_pin2));  // open: pin1, pin2, pin3, pin4, pin5, pin6
  bus_transceiver bus_transceiver_3 (
    .D0(n7486_4_pin8), .D1(n7486_4_pin11), .D2(n7486_4_pin6), .D3(n7486_4_pin3), .D4(n7486_5_pin8),
    .D5(n7486_5_pin11), .D6(n7486_5_pin6), .D7(n7486_5_pin3), .BUS_ENABLE(S_XOR), .Q0(bus_transceiver_1_q0),
    .Q1(bus_transceiver_1_q1), .Q2(bus_transceiver_1_q2), .Q3(bus_transceiver_1_q3),
    .Q4(bus_transceiver_1_q4), .Q5(bus_transceiver_1_q5), .Q6(bus_transceiver_1_q6), .Q7(bus_transceiver_1_q7));
  _7432 u_7432_4 (
    .pin13(n7408_4_pin11), .pin12(n7408_4_pin3), .pin11(n7486_7_pin4), .pin10(n7408_4_pin6),
    .pin9(n7408_4_pin8), .pin8(n7486_6_pin2));  // open: pin1, pin2, pin3, pin4, pin5, pin6
  _7432 u_7432_5 (
    .pin13(n7408_5_pin11), .pin12(n7408_5_pin3), .pin11(n7486_8_pin4), .pin10(n7408_5_pin6),
    .pin9(n7408_5_pin8), .pin8(n7486_7_pin2));  // open: pin1, pin2, pin3, pin4, pin5, pin6
  bus_transceiver bus_transceiver_4 (
    .D0(n7404_2_pin8), .D1(n7404_2_pin10), .D2(n7404_2_pin12), .D3(n7404_2_pin2), .D4(n7404_3_pin8),
    .D5(n7404_3_pin10), .D6(n7404_3_pin12), .D7(n7404_3_pin2), .BUS_ENABLE(S_NOT), .Q0(bus_transceiver_1_q0),
    .Q1(bus_transceiver_1_q1), .Q2(bus_transceiver_1_q2), .Q3(bus_transceiver_1_q3),
    .Q4(bus_transceiver_1_q4), .Q5(bus_transceiver_1_q5), .Q6(bus_transceiver_1_q6), .Q7(bus_transceiver_1_q7));
  _7432 u_7432_6 (
    .pin13(n7408_6_pin11), .pin12(n7408_6_pin3), .pin11(n7432_6_pin11), .pin10(n7408_6_pin6),
    .pin9(n7408_6_pin8), .pin8(n7486_8_pin2));  // open: pin1, pin2, pin3, pin4, pin5, pin6
  bus_transceiver bus_transceiver_5 (
    .D0(n7486_3_pin6), .D1(n7486_3_pin3), .D2(n7486_6_pin6), .D3(n7486_6_pin3), .D4(n7486_7_pin6),
    .D5(n7486_7_pin3), .D6(n7486_8_pin6), .D7(n7486_8_pin3), .BUS_ENABLE(CALC), .Q0(bus_transceiver_1_q0),
    .Q1(bus_transceiver_1_q1), .Q2(bus_transceiver_1_q2), .Q3(bus_transceiver_1_q3),
    .Q4(bus_transceiver_1_q4), .Q5(bus_transceiver_1_q5), .Q6(bus_transceiver_1_q6), .Q7(bus_transceiver_1_q7));
  xor xor_2 (xor_2_out, n7432_6_pin11, S_SUB);
  and and_1 (CARRY_FLAG, xor_2_out, CALC);
  bus_transceiver bus_transceiver_6 (
    .D0(bus_transceiver_1_q0), .D1(bus_transceiver_1_q1), .D2(bus_transceiver_1_q2),
    .D3(bus_transceiver_1_q3), .D4(bus_transceiver_1_q4), .D5(bus_transceiver_1_q5),
    .D6(bus_transceiver_1_q6), .D7(bus_transceiver_1_q7), .BUS_ENABLE(ALU_EN), .Q0(A[0]), .Q1(A[1]),
    .Q2(A[2]), .Q3(A[3]), .Q4(A[4]), .Q5(A[5]), .Q6(A[6]), .Q7(A[7]));
  nor nor_1 (nor_1_out, bus_transceiver_1_q0, bus_transceiver_1_q1, bus_transceiver_1_q2, bus_transceiver_1_q3);
  nor nor_2 (nor_2_out, bus_transceiver_1_q4, bus_transceiver_1_q5, bus_transceiver_1_q6, bus_transceiver_1_q7);
  and and_2 (ZERO_FLAG, nor_1_out, nor_2_out);

  // Other names for the same wires on the sheet: A_IS_ZERO = ZERO_FLAG; CARRY_OUT = CARRY_FLAG; Ctrl0 = ALU_CTRL0;
  //   Ctrl1 = ALU_CTRL1; Ctrl2 = ALU_CTRL2; A1 = X[1]; A2 = X[2]; A3 = X[3]; A4 = X[4]; A5 = X[5]; A6 = X[6];
  //   A7 = X[7]; B0 = Y[0]; B1 = Y[1]; B2 = Y[2]; B3 = Y[3]; B4 = Y[4]; B5 = Y[5]; B6 = Y[6]; B7 = Y[7]

  // Notes on the sheet:
  //   Y: initial=0x1
endmodule

module aluone (
  input  A,
  input  B,
  input  Cin,
  input  OPCODE0,
  input  OPCODE1,
  input  SUB,
  output CARRY_FLAG,
  output O,
  output ZERO_FLAG
);

  wire ADD_SUB_OUT, and_1_out, and_3_out, and_4_out, and_5_out, and_6_out, and_7_out, and_8_out, and_9_out,
       and_10_out, AND_OUT, not_1_out, not_2_out, or_1_out, or_2_out, or_4_out, or_5_out, or_6_out, OR_OUT,
       XOR_OUT;

  or or_1 (or_1_out, B, SUB);
  or or_2 (or_2_out, Cin, SUB);
  xor xor_1 (XOR_OUT, A, or_1_out);
  or or_3 (OR_OUT, A, B);
  xor xor_2 (ADD_SUB_OUT, XOR_OUT, or_2_out);
  and and_1 (and_1_out, XOR_OUT, or_2_out);
  and and_2 (AND_OUT, or_1_out, A);
  or or_4 (or_4_out, and_1_out, AND_OUT);
  xor xor_3 (CARRY_FLAG, or_4_out, SUB);
  not not_1 (not_1_out, OPCODE1);
  not not_2 (not_2_out, OPCODE0);
  and and_3 (and_3_out, not_1_out, not_2_out);
  and and_4 (and_4_out, not_1_out, OPCODE0);
  and and_5 (and_5_out, OPCODE1, not_2_out);
  and and_6 (and_6_out, OPCODE1, OPCODE0);
  and and_7 (and_7_out, ADD_SUB_OUT, and_3_out);
  and and_8 (and_8_out, AND_OUT, and_4_out);
  and and_9 (and_9_out, OR_OUT, and_5_out);
  and and_10 (and_10_out, XOR_OUT, and_6_out);
  or or_5 (or_5_out, and_7_out, and_8_out);
  or or_6 (or_6_out, and_9_out, and_10_out);
  or or_7 (O, or_5_out, or_6_out);
  xor xor_4 (ZERO_FLAG, O, 1'b1);
endmodule
